# Fritzing sketch PlanMorze (saved by Fritzing 0.9.2b)

parts:
  Часть1 = Arduino Nano (Rev3.0)
  R1 = Resistor [tolerance=±5% resistance=15k package=THT]
  LED1 = LED - 5mm [color="Green (560nm)" package="5 mm [THT]"]
  BC337-40 = NPN-Transistor [package="TO92 [THT]"]
  R2 = Resistor [tolerance=±5% resistance=330 package=THT]
  LED2 = LED - 5mm [color="Green (560nm)" package="5 mm [THT]"]
  LED3 = LED - 5mm [color="Green (560nm)" package="5 mm [THT]"]
  LED4 = LED - 5mm [color="Green (560nm)" package="5 mm [THT]"]
  LED5 = LED - 5mm [color="Green (560nm)" package="5 mm [THT]"]
  R3 = Resistor [tolerance=±5% resistance=15k package=THT]
  LED6 = LED - 5mm [color="Green (560nm)" package="5 mm [THT]"]
  LED7 = LED - 5mm [color="Green (560nm)" package="5 mm [THT]"]
  LED8 = LED - 5mm [color="Green (560nm)" package="5 mm [THT]"]
  LED9 = LED - 5mm [color="Green (560nm)" package="5 mm [THT]"]
  LED10 = LED - 5mm [color="Green (560nm)" package="5 mm [THT]"]
  BC337-40_2 = NPN-Transistor [package="TO92 [THT]"]
  R4 = Resistor [tolerance=±5% resistance=330 package=THT]
  R5 = Resistor [tolerance=±5% resistance=15k package=THT]
  LED11 = LED - 5mm [color="Green (560nm)" package="5 mm [THT]"]
  LED12 = LED - 5mm [color="Green (560nm)" package="5 mm [THT]"]
  LED13 = LED - 5mm [color="Green (560nm)" package="5 mm [THT]"]
  LED14 = LED - 5mm [color="Green (560nm)" package="5 mm [THT]"]
  LED15 = LED - 5mm [color="Green (560nm)" package="5 mm [THT]"]
  BC337-40_3 = NPN-Transistor [package="TO92 [THT]"]
  R6 = Resistor [tolerance=±5% resistance=330 package=THT]
  R7 = Resistor [tolerance=±5% resistance=15k package=THT]
  LED16 = LED - 5mm [color="Green (560nm)" package="5 mm [THT]"]
  LED17 = LED - 5mm [color="Green (560nm)" package="5 mm [THT]"]
  LED18 = LED - 5mm [color="Green (560nm)" package="5 mm [THT]"]
  LED19 = LED - 5mm [color="Green (560nm)" package="5 mm [THT]"]
  LED20 = LED - 5mm [color="Green (560nm)" package="5 mm [THT]"]
  BC337-40_4 = NPN-Transistor [package="TO92 [THT]"]
  R8 = Resistor [tolerance=±5% resistance=330 package=THT]
  S1 = Square Pushbutton
  LED21 = RGB LED (com. cathode, rgb) [package="5 mm [THT]"]
  C1 = Ceramic Capacitor [capacitance=10nF package="100 mil [THT, multilayer]"]
  R9 = Resistor [tolerance=±5% resistance=220 package=THT]
  R10 = Resistor [tolerance=±5% resistance=220 package=THT]

nets:
  N1: Часть1.D3, R1.Pin_0
  N2: Часть1.D4, S1.leg1, C1.1
  N3: Часть1.D5, R9.Pin_0
  N4: Часть1.D6, R10.Pin_0
  N5: Часть1.D9, R3.Pin_0
  N6: Часть1.D10, R5.Pin_0
  N7: Часть1.D11/MOSI, R7.Pin_0
  N8: R1.Pin_1, BC337-40.B
  N9: LED1.cathode, R2.Pin_0
  N10: LED1.anode, LED2.cathode
  GND: BC337-40.E, BC337-40_2.E, BC337-40_3.E, BC337-40_4.E, S1.leg0, LED21.common_cathode, C1.0
  N11: BC337-40.C, R2.Pin_1
  N12: LED2.anode, LED3.cathode
  N13: LED3.anode, LED4.cathode
  N14: LED4.anode, LED5.cathode
  12V: LED5.anode, LED8.anode, LED13.anode, LED18.anode
  N15: R3.Pin_1, BC337-40_2.B
  N16: LED6.cathode, LED7.anode
  N17: LED6.anode, LED10.cathode
  N18: LED7.cathode, R4.Pin_0
  N19: LED8.cathode, LED9.anode
  N20: LED9.cathode, LED10.anode
  N21: BC337-40_2.C, R4.Pin_1
  N22: R5.Pin_1, BC337-40_3.B
  N23: LED11.cathode, LED12.anode
  N24: LED11.anode, LED15.cathode
  N25: LED12.cathode, R6.Pin_0
  N26: LED13.cathode, LED14.anode
  N27: LED14.cathode, LED15.anode
  N28: BC337-40_3.C, R6.Pin_1
  N29: R7.Pin_1, BC337-40_4.B
  N30: LED16.cathode, LED17.anode
  N31: LED16.anode, LED20.cathode
  N32: LED17.cathode, R8.Pin_0
  N33: LED18.cathode, LED19.anode
  N34: LED19.cathode, LED20.anode
  N35: BC337-40_4.C, R8.Pin_1
  N36: LED21.red_anode, R10.Pin_1
  N37: LED21.blue_anode, R9.Pin_1
