# Fritzing sketch RU_01 (saved by Fritzing 0.9.2b)

parts:
  ArduinoMicro = Arduino Micro (Rev3)
  Ethernet_shield = Arduino Ethernet Shield (Rev3)
  R1 = Resistor [tolerance=±5% resistance=2.2k package=THT]
  Q1 = NPN-Transistor [part_number=2n222 package="TO92 [THT]"]
  RED1 = LED - 5mm [color="Red (633nm)" package="5 mm [THT]"]
  GR1 = LED - 5mm [color="Green (565nm)" package="5 mm [THT]"]
  Q2 = NPN-Transistor [part_number=2n222 package="TO92 [THT]"]
  R2 = Resistor [tolerance=±5% resistance=15k package="2010 [SMD]"]
  DD1 = Reed switch [package=THT]
  DD2 = Reed switch [package=THT]
  R4 = Resistor [tolerance=±5% resistance=15k package="2010 [SMD]"]
  R3 = Resistor [tolerance=±5% resistance=2.2k package=THT]
  Q3 = NPN-Transistor [part_number=2n222 package="TO92 [THT]"]
  Q4 = NPN-Transistor [part_number=2n222 package="TO92 [THT]"]
  RED12 = LED - 5mm [color="Red (633nm)" package="5 mm [THT]"]
  GR12 = LED - 5mm [color="Green (565nm)" package="5 mm [THT]"]
  NFC_0 = RFID-RC522-v2
  C1 = Ceramic Capacitor [capacitance=10nF package="100 mil [THT, multilayer]"]
  C2 = Ceramic Capacitor [capacitance=10nF package="100 mil [THT, multilayer]"]
  D1 = Schottky Diode [part_number=1N5817 breakdown_voltage=3.6V package="300 mil [THT]"]
  D2 = Schottky Diode [part_number=1N5817 breakdown_voltage=3.6V package="300 mil [THT]"]
  D3 = Schottky Diode [part_number=1N5817 breakdown_voltage=3.6V package="300 mil [THT]"]
  D4 = Schottky Diode [part_number=1N5817 breakdown_voltage=3.6V package="300 mil [THT]"]
  PIR2 = PIR sensor
  PIR1 = PIR sensor
  X1 = USB Connectors [package=usb-a-s-nosilk-female]
  D5 = Schottky Diode [part_number=1N5817 breakdown_voltage=3.6V package="300 mil [THT]"]
  D6 = Schottky Diode [part_number=1N5817 breakdown_voltage=3.6V package="300 mil [THT]"]
  D7 = Schottky Diode [part_number=1N5817 breakdown_voltage=3.6V package="300 mil [THT]"]
  D8 = Schottky Diode [part_number=1N5817 breakdown_voltage=3.6V package="300 mil [THT]"]
  R5 = Resistor [tolerance=±5% resistance=10k package=THT]
  C3 = Ceramic Capacitor [capacitance=10nF package="100 mil [THT, multilayer]"]
  DL1 = RELAY [package=relay-t9a]
  DL2 = RELAY [package=relay-t9a]
  C6 = Electrolytic Capacitor [capacitance=47µF voltage=20V package="300 mil [THT, electrolytic]"]
  C7 = Electrolytic Capacitor [capacitance=22µF voltage=50V package="300 mil [THT, electrolytic]"]

nets:
  N1: ArduinoMicro.MOSI, Ethernet_shield.ICSP_MOSI
  N2: ArduinoMicro.RESET, Ethernet_shield.RESET
  N3: ArduinoMicro.D2/SDA, NFC_0.SDA
  N4: ArduinoMicro.D3/SCL, NFC_0.SCK
  N5: ArduinoMicro.D4_PWM/A6, PIR1.SIG
  N6: ArduinoMicro.D5_PWM, PIR2.SIG
  N7: ArduinoMicro.D6_PWM/A7, X1.VBUS, D6.anode, D7.cathode, R5.Pin_1, C3.0
  N8: ArduinoMicro.D7, X1.D-, D5.anode, D8.cathode, C3.1
  N9: ArduinoMicro.D10_PWM/A10, Ethernet_shield.ETH_CS
  N10: ArduinoMicro.D11_PWM, DD1.pin_1, C2.1, D1.anode, D4.cathode
  N11: ArduinoMicro.D12_PWM/A11, DD2.pin_1, C1.1, D2.cathode, D3.anode
  N12: ArduinoMicro.SCK, Ethernet_shield.ICSP_SCK
  N13: ArduinoMicro.MISO, Ethernet_shield.ICSP_MISO
  N14: ArduinoMicro.A5, DL1.COIL1
  N15: ArduinoMicro.A4, DL2.COIL1
  N16: ArduinoMicro.A3, R4.Pin_0
  N17: ArduinoMicro.A2, R3.Pin_0
  N18: ArduinoMicro.A1, R2.Pin_0
  N19: ArduinoMicro.A0, R1.Pin_0
  N20: R1.Pin_1, Q1.B
  GND: Q1.E, Q2.E, DD1.pin_2, DD2.pin_2, Q3.E, Q4.E, C1.0, C2.0, D2.anode, D4.anode, X1.GND, D7.anode, D8.anode, R5.Pin_0, DL1.COIL2, DL2.COIL2, C6.-, C7.-
  N21: Q1.C, RED1.cathode
  12V: RED1.anode, GR1.anode, RED12.anode, GR12.anode, C6.+
  N22: GR1.cathode, Q2.C
  N23: Q2.B, R2.Pin_1
  N24: R4.Pin_1, Q3.B
  N25: R3.Pin_1, Q4.B
  N26: Q3.C, GR12.cathode
  N27: Q4.C, RED12.cathode
  5V: D1.cathode, D3.cathode, X1.D+, D5.cathode, D6.cathode, C7.+

custom parts:
  RFID-RC522-v2: A simple China made RFID-RC522 Reader; do check the pin labels, as this is a MFRC522 based clone.
