# Fritzing sketch RU_03 (saved by Fritzing 0.9.3b)

parts:
  Ethernet = Arduino Ethernet Shield (Rev3)
  RU_03 = Arduino Micro (Rev3)
  U1 = HC-SR04 [chip_label=IC package="SIP (Single Inline) [THT]"]
  R3 = Resistor [tolerance=±5% resistance=15k package="2010 [SMD]"]
  R4 = Resistor [tolerance=±5% resistance=2.2k package=THT]
  Q3 = NPN-Transistor [part_number=2n222 package="TO92 [THT]"]
  Q4 = NPN-Transistor [part_number=2n222 package="TO92 [THT]"]
  RED34a = LED - 5mm [color="Red (633nm)" package="5 mm [THT]"]
  GR34a = LED - 5mm [color="Green (565nm)" package="5 mm [THT]"]
  R5 = Resistor [tolerance=±5% resistance=15k package="2010 [SMD]"]
  R6 = Resistor [tolerance=±5% resistance=2.2k package=THT]
  Q5 = NPN-Transistor [part_number=2n222 package="TO92 [THT]"]
  Q6 = NPN-Transistor [part_number=2n222 package="TO92 [THT]"]
  RED34b = LED - 5mm [color="Red (633nm)" package="5 mm [THT]"]
  GR34b = LED - 5mm [color="Green (565nm)" package="5 mm [THT]"]
  DL34b = RELAY [package=relay-t9a]
  DL34a = RELAY [package=relay-t9a]
  C2 = Ceramic Capacitor [capacitance=10nF package="100 mil [THT, multilayer]"]
  D3 = Schottky Diode [part_number=1N5817 breakdown_voltage=3.6V package="300 mil [THT]"]
  D4 = Schottky Diode [part_number=1N5817 breakdown_voltage=3.6V package="300 mil [THT]"]
  DD34b = Reed switch [package=THT]
  C3 = Ceramic Capacitor [capacitance=10nF package="100 mil [THT, multilayer]"]
  D5 = Schottky Diode [part_number=1N5817 breakdown_voltage=3.6V package="300 mil [THT]"]
  D6 = Schottky Diode [part_number=1N5817 breakdown_voltage=3.6V package="300 mil [THT]"]
  DD34a = Reed switch [package=THT]
  C4 = Ceramic Capacitor [capacitance=10nF package="100 mil [THT, multilayer]"]
  D7 = Schottky Diode [part_number=1N5817 breakdown_voltage=3.6V package="300 mil [THT]"]
  D8 = Schottky Diode [part_number=1N5817 breakdown_voltage=3.6V package="300 mil [THT]"]
  PowerCable = Square Pushbutton
  DLcombox = RELAY [package=relay-t9a]
  C5 = Ceramic Capacitor [capacitance=10nF package="100 mil [THT, multilayer]"]
  D9 = Schottky Diode [part_number=1N5817 breakdown_voltage=3.6V package="300 mil [THT]"]
  D10 = Schottky Diode [part_number=1N5817 breakdown_voltage=3.6V package="300 mil [THT]"]
  TruncButton = Square Pushbutton
  R13 = Resistor [tolerance=±5% resistance=220 package=THT]
  TruncLED = LED - 5mm [color="Green (560nm)" package="5 mm [THT]"]
  DLRedAlert = RELAY [package=relay-t9a]

nets:
  N1: Ethernet.ICSP_MISO, RU_03.MISO
  N2: Ethernet.ICSP_SCK, RU_03.SCK
  N3: Ethernet.ICSP_MOSI, RU_03.MOSI
  N4: Ethernet.RESET, RU_03.RESET
  N5: Ethernet.ETH_CS, RU_03.D10_PWM/A10
  N6: RU_03.D2/SDA, U1.Trig
  N7: RU_03.D3/SCL, U1.Echo
  N8: RU_03.D4_PWM/A6, DLcombox.COIL1
  N9: RU_03.D5_PWM, C2.1, D3.anode, D4.cathode, DD34b.pin_1
  N10: RU_03.D6_PWM/A7, C3.1, D5.anode, D6.cathode, DD34a.pin_1
  N11: RU_03.D7, C4.1, D7.anode, D8.cathode, PowerCable.leg1
  N12: RU_03.D8_PWM/A8, C5.1, D9.anode, D10.cathode, TruncButton.leg1
  N13: RU_03.D9_PWM/A9, R13.Pin_0
  N14: RU_03.D11_PWM, DLRedAlert.COIL1
  N15: RU_03.A5, DL34b.COIL1
  N16: RU_03.A4, DL34a.COIL1
  N17: RU_03.A3, R5.Pin_0
  N18: RU_03.A2, R6.Pin_0
  N19: RU_03.A1, R3.Pin_0
  N20: RU_03.A0, R4.Pin_0
  N21: R3.Pin_1, Q3.B
  N22: R4.Pin_1, Q4.B
  GND: Q3.E, Q4.E, Q5.E, Q6.E, DL34b.COIL2, DL34a.COIL2, C2.0, D4.anode, DD34b.pin_2, C3.0, D6.anode, DD34a.pin_2, C4.0, D8.anode, PowerCable.leg0, DLcombox.COIL2, C5.0, D10.anode, TruncButton.leg0, TruncLED.cathode, DLRedAlert.COIL2
  N23: Q3.C, GR34a.cathode
  N24: Q4.C, RED34a.cathode
  12V: RED34a.anode, GR34a.anode, RED34b.anode, GR34b.anode
  N25: R5.Pin_1, Q5.B
  N26: R6.Pin_1, Q6.B
  N27: Q5.C, GR34b.cathode
  N28: Q6.C, RED34b.cathode
  5V: D3.cathode, D5.cathode, D7.cathode, D9.cathode
  N29: R13.Pin_1, TruncLED.anode

custom parts:
  HC-SR04: HC-SR04 ultrasound distance sensor
