# Fritzing sketch RU_04 (saved by Fritzing 0.9.3b)

parts:
  Ethernet = Arduino Ethernet Shield (Rev3)
  RU_03 = Arduino Micro (Rev3)
  DLT = RELAY [package=relay-t9a]
  DLW = RELAY [package=relay-t9a]
  C2 = Ceramic Capacitor [capacitance=10nF package="100 mil [THT, multilayer]"]
  D3 = Schottky Diode [part_number=1N5817 breakdown_voltage=3.6V package="300 mil [THT]"]
  D4 = Schottky Diode [part_number=1N5817 breakdown_voltage=3.6V package="300 mil [THT]"]
  DDT = Reed switch [package=THT]
  R9 = Resistor [tolerance=±5% resistance=10k package=THT]
  R10 = Resistor [tolerance=±5% resistance=10k package=THT]
  R11 = Resistor [tolerance=±5% resistance=10k package=THT]
  C6 = Ceramic Capacitor [capacitance=10nF package="100 mil [THT, multilayer]"]
  C7 = Ceramic Capacitor [capacitance=10nF package="100 mil [THT, multilayer]"]
  C8 = Ceramic Capacitor [capacitance=10nF package="100 mil [THT, multilayer]"]
  D14 = Rectifier Diode [part_number=1N4148 package="300 mil [THT]"]
  D15 = Rectifier Diode [part_number=1N4148 package="300 mil [THT]"]
  D16 = Rectifier Diode [part_number=1N4148 package="300 mil [THT]"]
  D17 = Rectifier Diode [part_number=1N4148 package="300 mil [THT]"]
  D18 = Rectifier Diode [part_number=1N4148 package="300 mil [THT]"]
  D19 = Rectifier Diode [part_number=1N4148 package="300 mil [THT]"]
  D20 = Rectifier Diode [part_number=1N4148 package="300 mil [THT]"]
  D21 = Rectifier Diode [part_number=1N4148 package="300 mil [THT]"]
  D22 = Rectifier Diode [part_number=1N4148 package="300 mil [THT]"]
  Key2GreenLed = LED - 5mm [color="Green (560nm)" package="5 mm [THT]"]
  Key1GreenLed = LED - 5mm [color="Green (560nm)" package="5 mm [THT]"]
  Key0GreenLed = LED - 5mm [color="Green (560nm)" package="5 mm [THT]"]
  R12 = Resistor [tolerance=±5% resistance=220 package=THT]
  R13 = Resistor [tolerance=±5% resistance=220 package=THT]
  R14 = Resistor [tolerance=±5% resistance=220 package=THT]
  Key2 = Square Pushbutton
  Key1 = Square Pushbutton
  Key0 = Square Pushbutton
  Key2RedLed = LED - 5mm [color="Red (635nm)" package="5 mm [THT]"]
  Key1RedLed = LED - 5mm [color="Red (635nm)" package="5 mm [THT]"]
  Key0RedLed = LED - 5mm [color="Red (635nm)" package="5 mm [THT]"]
  R15 = Resistor [tolerance=±5% resistance=220 package=THT]
  R16 = Resistor [tolerance=±5% resistance=220 package=THT]
  R17 = Resistor [tolerance=±5% resistance=220 package=THT]
  R18 = Resistor [tolerance=±5% resistance=10k package=THT]
  C9 = Ceramic Capacitor [capacitance=10nF package="100 mil [THT, multilayer]"]
  D23 = Rectifier Diode [part_number=1N4148 package="300 mil [THT]"]
  D24 = Rectifier Diode [part_number=1N4148 package="300 mil [THT]"]
  D25 = Rectifier Diode [part_number=1N4148 package="300 mil [THT]"]
  Key3 = Square Pushbutton
  Key3GreenLed = LED - 5mm [color="Green (560nm)" package="5 mm [THT]"]
  R19 = Resistor [tolerance=±5% resistance=220 package=THT]
  Key3RedLed = LED - 5mm [color="Red (635nm)" package="5 mm [THT]"]
  R20 = Resistor [tolerance=±5% resistance=220 package=THT]

nets:
  N1: Ethernet.ICSP_MISO, RU_03.MISO
  N2: Ethernet.ICSP_SCK, RU_03.SCK
  N3: Ethernet.ICSP_MOSI, RU_03.MOSI
  N4: Ethernet.RESET, RU_03.RESET
  N5: Ethernet.ETH_CS, RU_03.D10_PWM/A10
  N6: RU_03.D1/TX, R13.Pin_0
  N7: RU_03.D0/RX, R14.Pin_0
  N8: RU_03.D2/SDA, R12.Pin_0
  N9: RU_03.D3/SCL, R11.Pin_1, C8.0, D17.anode, D22.cathode, Key0.leg0
  N10: RU_03.D4_PWM/A6, C8.1, D16.anode, D17.cathode, Key0.leg1
  N11: RU_03.D5_PWM, R10.Pin_1, C7.0, D20.anode, D21.cathode, Key1.leg0
  N12: RU_03.D6_PWM/A7, C7.1, D15.anode, D20.cathode, Key1.leg1
  N13: RU_03.D7, R9.Pin_1, C6.0, D18.anode, D19.cathode, Key2.leg0
  N14: RU_03.D8_PWM/A8, C6.1, D14.anode, D18.cathode, Key2.leg1
  N15: RU_03.D9_PWM/A9, R18.Pin_1, C9.0, D24.anode, D25.cathode, Key3.leg0
  N16: RU_03.D11_PWM, C9.1, D23.anode, D24.cathode, Key3.leg1
  N17: RU_03.D12_PWM/A11, R19.Pin_0
  N18: RU_03.A5, DLT.COIL1
  N19: RU_03.A4, DLW.COIL1
  N20: RU_03.A3, C2.1, D3.anode, D4.cathode, DDT.pin_1
  N21: RU_03.A2, R15.Pin_0
  N22: RU_03.A1, R16.Pin_0
  N23: RU_03.A0, R17.Pin_0
  N24: RU_03.D13_PWM, R20.Pin_0
  GND: DLT.COIL2, DLW.COIL2, C2.0, D4.anode, DDT.pin_2, R9.Pin_0, R10.Pin_0, R11.Pin_0, D19.anode, D21.anode, D22.anode, Key2GreenLed.cathode, Key1GreenLed.cathode, Key0GreenLed.cathode, Key2RedLed.cathode, Key1RedLed.cathode, Key0RedLed.cathode, R18.Pin_0, D25.anode, Key3GreenLed.cathode, Key3RedLed.cathode
  5V: D3.cathode, D14.cathode, D15.cathode, D16.cathode, D23.cathode
  N25: Key2GreenLed.anode, R12.Pin_1
  N26: Key1GreenLed.anode, R13.Pin_1
  N27: Key0GreenLed.anode, R14.Pin_1
  N28: Key2RedLed.anode, R15.Pin_1
  N29: Key1RedLed.anode, R16.Pin_1
  N30: Key0RedLed.anode, R17.Pin_1
  N31: Key3GreenLed.anode, R19.Pin_1
  N32: Key3RedLed.anode, R20.Pin_1
